# Fritzing sketch Untitled Sketch (saved by Fritzing 0.8.7b)
breadboards: 1

parts:
  PIC_16F877A2 = PICAXE-18 [part_number="poc " package=THT]
  LED1 = LED - 5mm [color="Red (633nm)" package="5 mm [THT]"]
  LED2 = LED - 5mm [color="Yellow (595nm)" package="5 mm [THT]"]
  LED3 = LED - 5mm [color="Green (555nm)" package="5 mm [THT]"]
  LED4 = LED - 5mm [color="Red (633nm)" package="5 mm [THT]"]
  LED5 = LED - 5mm [color="Green (555nm)" package="5 mm [THT]"]
  XTAL1 = Crystal [frequency="16 Mhz" package=THT]
  R1 = Resistor [tolerance=±5% resistance=330 package=THT]
  R2 = Resistor [tolerance=±5% resistance=330 package=THT]
  R3 = Resistor [tolerance=±5% resistance=330 package=THT]
  R4 = Resistor [tolerance=±5% resistance=330 package=THT]
  R5 = Resistor [tolerance=±5% resistance=330 package=THT]
  S1 = Pushbutton [package="[THT]"]
  R6 = Resistor [tolerance=±5% resistance=1k package=THT]
  S2 = Pushbutton [package="[THT]"]
  R7 = Resistor [tolerance=±5% resistance=1k package=THT]
  LED6 = LED - 5mm [color="Red (633nm)" package="5 mm [THT]"]
  LED7 = LED - 5mm [color="Yellow (595nm)" package="5 mm [THT]"]
  LED8 = LED - 5mm [color="Green (555nm)" package="5 mm [THT]"]
  LED9 = LED - 5mm [color="Red (633nm)" package="5 mm [THT]"]
  LED10 = LED - 5mm [color="Green (555nm)" package="5 mm [THT]"]
  R9 = Resistor [tolerance=±5% resistance=330 package=THT]
  R10 = Resistor [tolerance=±5% resistance=330 package=THT]
  R11 = Resistor [tolerance=±5% resistance=330 package=THT]
  R12 = Resistor [tolerance=±5% resistance=220 package=THT]
  R13 = Resistor [tolerance=±5% resistance=330 package=THT]
  U1 = Voltage Regulator - 5V [package="TO220 [THT]"]
  C1 = Electrolytic Capacitor [capacitance=1µF package="100 mil [THT, electrolytic]"]
  VCC1 = Battery block 9V

nets:
  N1: PIC_16F877A2.In_2, C1.+
  N2: PIC_16F877A2.Reset, PIC_16F877A2.Out_1, PIC_16F877A2.Out_5, PIC_16F877A2.Out_6, PIC_16F877A2.Out_7, PIC_16F877A2.In_7, PIC_16F877A2.In_0, PIC_16F877A2.In_1, LED1.cathode, LED2.cathode, LED3.cathode, LED4.cathode, LED5.cathode, S1.Pin_1, S1.Pin_2, R6.Pin_1, S2.Pin_1, S2.Pin_2, LED6.cathode, LED7.cathode, LED8.cathode, LED9.cathode, R9.Pin_1, R13.Pin_0, U1.GND, C1.-, VCC1.-
  N3: PIC_16F877A2.0V, PIC_16F877A2.+V, LED7.anode, R10.Pin_1
  N4: PIC_16F877A2.Out_0, XTAL1.pin_0
  N5: PIC_16F877A2.Out_2, PIC_16F877A2.Out_4, R6.Pin_0, R7.Pin_1, U1.output_voltage
  N6: PIC_16F877A2.Out_3, R11.Pin_0
  N7: LED1.anode, R1.Pin_1
  N8: LED2.anode, R2.Pin_1
  N9: LED3.anode, R3.Pin_1
  N10: LED4.anode, R4.Pin_1
  N11: LED5.anode, R5.Pin_1
  N12: S2.Pin_3, S2.Pin_4
  N13: LED8.anode, R11.Pin_1
  N14: LED10.anode, R12.Pin_1
  N15: U1.input_voltage, VCC1.+
